// Digital circuit 4bit_MemoryModule.dig as structural Verilog
module _4bit_MemoryModule (
  input  [3:0] Data,
  input  [3:0] Write_Address,
  input  [3:0] Read_Input,
  input  Clock,
  output [3:0] Output
);

  wire [3:0] demultiplexer_1_out_0, demultiplexer_1_out_1, demultiplexer_1_out_2, demultiplexer_1_out_3,
       demultiplexer_1_out_4, demultiplexer_1_out_5, demultiplexer_1_out_6, demultiplexer_1_out_7,
       demultiplexer_1_out_8, demultiplexer_1_out_9, demultiplexer_1_out_10, demultiplexer_1_out_11,
       demultiplexer_1_out_12, demultiplexer_1_out_13, demultiplexer_1_out_14, demultiplexer_1_out_15,
       register_1_p3, register_2_p3, register_3_p3, register_4_p3, register_5_p3, register_6_p3,
       register_7_p3, register_8_p3, register_9_p3, register_10_p3, register_11_p3, register_13_p3,
       register_14_p3, register_15_p3, register_16_p3;

  Demultiplexer #(.Bits(4), .Selector_Bits(4)) demultiplexer_1 (
    .sel(Write_Address), .in(Data), .out_0(demultiplexer_1_out_0), .out_1(demultiplexer_1_out_1),
    .out_2(demultiplexer_1_out_2), .out_3(demultiplexer_1_out_3), .out_4(demultiplexer_1_out_4),
    .out_5(demultiplexer_1_out_5), .out_6(demultiplexer_1_out_6), .out_7(demultiplexer_1_out_7),
    .out_8(demultiplexer_1_out_8), .out_9(demultiplexer_1_out_9), .out_10(demultiplexer_1_out_10),
    .out_11(demultiplexer_1_out_11), .out_12(demultiplexer_1_out_12), .out_13(demultiplexer_1_out_13),
    .out_14(demultiplexer_1_out_14), .out_15(demultiplexer_1_out_15));
  // Register register_1: pin names not known; wires that end beside it: Clock, demultiplexer_1_out_0, register_1_p3
  // Register register_2: pin names not known; wires that end beside it: Clock, demultiplexer_1_out_1, register_2_p3
  // Register register_3: pin names not known; wires that end beside it: Clock, demultiplexer_1_out_2, register_3_p3
  // Register register_4: pin names not known; wires that end beside it: Clock, demultiplexer_1_out_3, register_4_p3
  // Register register_5: pin names not known; wires that end beside it: Clock, demultiplexer_1_out_4, register_5_p3
  // Register register_6: pin names not known; wires that end beside it: Clock, demultiplexer_1_out_5, register_6_p3
  // Register register_7: pin names not known; wires that end beside it: Clock, demultiplexer_1_out_6, register_7_p3
  // Register register_8: pin names not known; wires that end beside it: Clock, demultiplexer_1_out_7, register_8_p3
  // Register register_9: pin names not known; wires that end beside it: Clock, demultiplexer_1_out_8, register_9_p3
  // Register register_10: pin names not known; wires that end beside it: Clock, demultiplexer_1_out_9, register_10_p3
  // Register register_11: pin names not known; wires that end beside it: Clock, demultiplexer_1_out_10, register_11_p3
  // Register register_12: pin names not known; wires that end beside it: Clock, demultiplexer_1_out_11, register_11_p3
  // Register register_13: pin names not known; wires that end beside it: Clock, demultiplexer_1_out_12, register_13_p3
  // Register register_14: pin names not known; wires that end beside it: Clock, demultiplexer_1_out_13, register_14_p3
  // Register register_15: pin names not known; wires that end beside it: Clock, demultiplexer_1_out_14, register_15_p3
  // Register register_16: pin names not known; wires that end beside it: Clock, demultiplexer_1_out_15, register_16_p3
  Multiplexer #(.Selector_Bits(4), .Bits(4)) multiplexer_1 (
    .sel(Read_Input), .in_0(register_1_p3), .in_1(register_2_p3), .in_2(register_3_p3), .in_3(register_4_p3),
    .in_4(register_5_p3), .in_5(register_6_p3), .in_6(register_7_p3), .in_7(register_8_p3),
    .in_8(register_9_p3), .in_9(register_10_p3), .in_10(register_11_p3), .in_11(register_11_p3),
    .in_12(register_13_p3), .in_13(register_14_p3), .in_14(register_15_p3), .in_15(register_16_p3),
    .out(Output));
endmodule
